// Logisim project alu.circ as structural Verilog: 1 circuit, main circuit main
module main (
  input  [31:0] X,
  input  [31:0] Y,
  input  [5:0] Switch__S,
  output Signed_Overflow,
  output [31:0] RESULT,
  output Equal
);

  wire add_overflow, adder_1_cout, comparator_1_lt, comparator_2_lt, comparator_3_eq, comparator_4_eq,
       comparator_5_eq, sub_overflow, subtractor_1_bout, xor_1_out, xor_2_out, xor_3_out;
  wire [31:0] adder_1_out, and_2_out, bit_extender_1_out, bit_extender_2_out, bit_extender_3_out,
       bit_extender_4_out, multiplexer_1_out, multiplexer_2_out, or_1_out, or_2_out, shifter_1_out,
       shifter_2_out, shifter_3_out, shifter_4_out, shifter_5_out, subtractor_1_out;

  // Probe on X[15:0]
  Shifter #(.width(32), .shift("lr")) shifter_1 (.in(X), .\dist (5'b00001), .out(shifter_1_out));
  xor xor_1 (xor_1_out, X[0], X[2]);
  xor xor_2 (xor_2_out, xor_1_out, X[3]);
  Comparator #(.width(32)) comparator_1 (.a(X), .b(Y), .lt(comparator_1_lt));  // open: gt, eq
  Comparator #(.width(32), .mode("unsigned")) comparator_2 (
    .a(X), .b(Y), .eq(Equal), .lt(comparator_2_lt));  // open: gt
  // Probe on {X[0], X[1], X[2], X[3], X[4], X[5], X[6], X[7], X[8], X[9], X[10], X[11], X[12], X[13], X[14], X[15]}
  xor xor_3 (xor_3_out, xor_2_out, X[5]);
  assign bit_extender_1_out = {{31{1'b0}}, xor_3_out};  // Bit_Extender bit_extender_1
  Shifter #(.width(32)) shifter_2 (.in(X), .\dist (Y[4:0]), .out(shifter_2_out));
  Shifter #(.width(32), .shift("lr")) shifter_3 (.in(X), .\dist (Y[4:0]), .out(shifter_3_out));
  Shifter #(.width(32), .shift("ar")) shifter_4 (.in(X), .\dist (Y[4:0]), .out(shifter_4_out));
  and and_1 (add_overflow, comparator_3_eq, adder_1_cout);
  Comparator #(.width(6), .mode("unsigned")) comparator_3 (
    .a(Switch__S), .b(6'b100000), .eq(comparator_3_eq));  // open: gt, lt
  Adder #(.width(32)) adder_1 (.a(X), .b(Y), .out(adder_1_out), .cout(adder_1_cout));  // open: cin
  Subtractor #(.width(32)) subtractor_1 (.a(X), .b(Y), .out(subtractor_1_out), .bout(subtractor_1_bout));  // open: bin
  assign and_2_out = X & Y;  // AND_Gate and_2, 32 bits wide
  assign or_1_out = X | Y;  // OR_Gate or_1, 32 bits wide
  assign bit_extender_2_out = {{31{1'b0}}, comparator_1_lt};  // Bit_Extender bit_extender_2
  assign bit_extender_3_out = {{31{1'b0}}, comparator_2_lt};  // Bit_Extender bit_extender_3
  Comparator #(.width(16)) comparator_4 (
    .a({X[0], X[1], X[2], X[3], X[4], X[5], X[6], X[7], X[8], X[9], X[10], X[11], X[12], X[13], X[14], X[15]}),
    .b(X[31:16]), .eq(comparator_4_eq));  // open: gt, lt
  Shifter #(.width(32)) shifter_5 (.in(bit_extender_1_out), .\dist (5'b01111), .out(shifter_5_out));
  assign bit_extender_4_out = {{31{1'b0}}, comparator_4_eq};  // Bit_Extender bit_extender_4
  assign or_2_out = shifter_1_out | shifter_5_out;  // OR_Gate or_2, 32 bits wide
  Multiplexer #(.select(5), .width(32), .enable("false")) multiplexer_1 (
    .in0(shifter_2_out), .in2(shifter_3_out), .in3(shifter_4_out), .out(multiplexer_1_out),
    .sel(Switch__S[4:0]));  // open: in1, in4, in5, in6, in7, in8, in9, in10, in11, in12, in13, in14, in15, in16, in17, in18, in19, in20, in21, in22, in23, in24, in25, in26, in27, in28, in29, in30, in31
  and and_3 (sub_overflow, comparator_5_eq, subtractor_1_bout);
  Comparator #(.width(6), .mode("unsigned")) comparator_5 (
    .a(Switch__S), .b(6'b100010), .eq(comparator_5_eq));  // open: gt, lt
  Multiplexer #(.select(5), .width(32), .enable("false")) multiplexer_2 (
    .in0(adder_1_out), .in1(adder_1_out), .in2(subtractor_1_out), .in3(subtractor_1_out), .in4(and_2_out),
    .in5(or_1_out), .in10(bit_extender_2_out), .in11(bit_extender_3_out), .in30(bit_extender_4_out),
    .in31(or_2_out), .out(multiplexer_2_out), .sel(Switch__S[4:0]));  // open: in6, in7, in8, in9, in12, in13, in14, in15, in16, in17, in18, in19, in20, in21, in22, in23, in24, in25, in26, in27, in28, in29
  Multiplexer #(.width(32), .enable("false")) multiplexer_3 (
    .in0(multiplexer_1_out), .in1(multiplexer_2_out), .out(RESULT), .sel(Switch__S[5]));
  or or_3 (Signed_Overflow, add_overflow, sub_overflow);
  // Probe on X[0]
  // Probe on X[15]
  // Probe on X[15]
  // Probe on X[0]

  // Other names for the same wires on the sheet: Eq = Equal; Func[5:0] = Switch__S; Select[4:0] = Switch__S[4:0];
  //   Select__2 = Switch__S[5]; _15 = X[15]; Reverse_input[15:0] = X[15:0];
  //   Reverse_output[15:0] = {X[0], X[1], X[2], X[3], X[4], X[5], X[6], X[7], X[8], X[9], X[10], X[11], X[12], X[13], X[14], X[15]};
  //   _14 = X[14]; _13 = X[13]; _12 = X[12]; _11 = X[11]; _10 = X[10]; _9 = X[9]; _8 = X[8]; _7 = X[7]; _6 = X[6];
  //   _5 = X[5]; _4 = X[4]; _3 = X[3]; _2 = X[2]; _1 = X[1]; _0 = X[0]

  // Notes on the sheet:
  //   INPUTS to your circuit
  //   INPUT to your circuit
  //   DON'T CHANGE THE INPUTS AND OUTPUTS! IF YOU DO SO, YOU NEED TO MAKE SURE THE PINS ARE IN THE RIGHT PLACES!
  //   16-bit reverser
  //   OUTPUTS of your circuit
endmodule
