// Logisim project cpu.circ as structural Verilog: 1 circuit, main circuit main
module main (
  input  [31:0] RS_READ_VALUE,
  input  [31:0] RT_READ_VALUE,
  input  [31:0] INSTRUCTION,
  input  CLOCK,
  input  RESET,
  output [31:0] t0,
  output [31:0] t1,
  output [31:0] t2,
  output [31:0] t3,
  output [4:0] RS,
  output [4:0] RT,
  output [4:0] Write_Register,
  output [31:0] RD_WRITE_VALUE,
  output RD_WRITE_ENABLE,
  output [23:0] FETCH_ADDRESS
);

  wire and_1_out, comparator_1_eq, comparator_2_eq, MEM_p1, MEM_p3;
  wire [5:0] ALU_Func, bit_extender_1_out;
  wire [23:0] adder_1_out, PC_q;
  wire [31:0] ALU_result, main_1_read_data_1, main_1_read_data_2;

  Adder #(.width(24)) adder_1 (.a(24'h1), .b(PC_q), .out(adder_1_out));  // open: cin, cout
  Register #(.width(24)) PC (.D(adder_1_out), .en(1'b1), .Q(PC_q), .clk(CLOCK));  // open: clr
  Adder #(.width(24)) adder_2 (.a(PC_q), .b(24'h400000), .out(FETCH_ADDRESS));  // open: cin, cout
  Comparator #(.width(6)) comparator_1 (.a(INSTRUCTION[31:26]), .b({6{1'b0}}), .eq(comparator_1_eq));  // open: gt, lt
  Comparator #(.width(4)) comparator_2 (.a(INSTRUCTION[5:2]), .b(4'b0000), .eq(comparator_2_eq));  // open: gt, lt
  assign bit_extender_1_out = {{1{1'b0}}, INSTRUCTION[10:6]};  // Bit_Extender bit_extender_1
  and and_1 (and_1_out, comparator_1_eq, comparator_2_eq);
  // mem_main MEM: pin names not known; wires that end beside it: MEM_p1, MEM_p1, MEM_p3
  regfile_main main_1 (
    .Read_register_1(INSTRUCTION[22:21]), .Read_register_2(INSTRUCTION[17:16]),
    .write_register(INSTRUCTION[12:11]), .write_data(ALU_result), .t0_Value(t0), .t1_Value(t1),
    .t2_Value(t2), .t3_Value(t3), .RegWrite(1'b1), .clock(CLOCK), .Read_Data_1(main_1_read_data_1),
    .Read_Data_2(main_1_read_data_2));
  Multiplexer #(.width(6), .enable("false")) multiplexer_1 (
    .in0(INSTRUCTION[5:0]), .in1(bit_extender_1_out), .out(ALU_Func), .sel(and_1_out));
  alu_main ALU (
    .Switch__S(ALU_Func), .X(main_1_read_data_1), .RESULT(ALU_result), .Y(main_1_read_data_2));  // open: Equal, Signed_Overflow

  // Other names for the same wires on the sheet: CLK = CLOCK; Func[5:0] = INSTRUCTION[5:0];
  //   Shamt[4:0] = INSTRUCTION[10:6]; Rd[1:0] = INSTRUCTION[12:11]; Rt_t[1:0] = INSTRUCTION[17:16];
  //   Rs_t[1:0] = INSTRUCTION[22:21]; OpCode[5:0] = INSTRUCTION[31:26]

  // Notes on the sheet:
  //   Word-addressed
  //   Text Segment Start
  //   These are outputs/inputs from run.circ
  //   Determine which ALU function to use
  //   Feel free to move these components
  //   RegFile
  //   These are outputs to run.circ
endmodule
