// Logisim project run.circ as structural Verilog: 1 circuit, main circuit main
module main (
  output [31:0] t0,
  output [31:0] t1,
  output [31:0] t2,
  output [31:0] t3,
  output [23:0] Clock_Count
);

  wire clock_1_out, RD_WRITE_ENABLE;
  wire [4:0] RD, RS, RT;
  wire [23:0] adder_1_out, FETCH_ADDRESS;
  wire [31:0] INSTRUCTION, RD_WRITE_VALUE, RS_READ_VALUE, RT_READ_VALUE;

  // Probe on FETCH_ADDRESS
  ROM #(.addrWidth(24), .dataWidth(32)) rom_1 (.addr(FETCH_ADDRESS), .data(INSTRUCTION));  // open: sel
  // Probe on INSTRUCTION
  Clock clock_1 (.out(clock_1_out));
  cpu_main CPU (
    .RS_READ_VALUE(RS_READ_VALUE), .RT_READ_VALUE(RT_READ_VALUE), .INSTRUCTION(INSTRUCTION),
    .CLOCK(clock_1_out), .RS(RS), .RT(RT), .Write_Register(RD), .RD_WRITE_VALUE(RD_WRITE_VALUE),
    .RD_WRITE_ENABLE(RD_WRITE_ENABLE), .FETCH_ADDRESS(FETCH_ADDRESS), .t0(t0), .t1(t1), .t2(t2), .t3(t3));  // open: RESET
  Register #(.width(24)) register_1 (.D(adder_1_out), .Q(Clock_Count), .clk(clock_1_out));  // open: en, clr
  Adder #(.width(24)) adder_1 (.a(24'h1), .b(Clock_Count), .out(adder_1_out));  // open: cin, cout

  // Notes on the sheet:
  //   contents of rom_1 (hex, n*v repeats v):
  //   4194304*0 83e 2
endmodule
